// Logisim project Joystick-led-mux.circ as structural Verilog: 1 circuit, main circuit main
module main (
);

  wire [2:0] joystick_1_x, joystick_1_y;
  wire [6:0] decoder_1_out1, decoder_2_out7, multiplexer_1_out, multiplexer_2_out;

  Joystick #(.bits(3)) joystick_1 (.x(joystick_1_x), .y(joystick_1_y));
  Decoder #(.select(3)) decoder_1 (
    .out1(decoder_1_out1[0]), .out2(decoder_1_out1[1]), .out3(decoder_1_out1[2]), .out4(decoder_1_out1[3]),
    .out5(decoder_1_out1[4]), .out6(decoder_1_out1[5]), .out7(decoder_1_out1[6]), .sel(joystick_1_x),
    .en(1'b1));  // open: out0
  Decoder #(.select(3)) decoder_2 (
    .out1(decoder_2_out7[6]), .out2(decoder_2_out7[5]), .out3(decoder_2_out7[4]), .out4(decoder_2_out7[3]),
    .out5(decoder_2_out7[2]), .out6(decoder_2_out7[1]), .out7(decoder_2_out7[0]), .sel(joystick_1_y),
    .en(1'b1));  // open: out0
  Multiplexer #(.select(3), .width(7), .enable("false")) multiplexer_1 (
    .in1(decoder_1_out1), .in2(decoder_1_out1), .in3(decoder_1_out1), .in4(decoder_1_out1),
    .in5(decoder_1_out1), .in6(decoder_1_out1), .in7(decoder_1_out1), .out(multiplexer_1_out),
    .sel(joystick_1_x));  // open: in0
  Multiplexer #(.select(3), .width(7), .enable("false")) multiplexer_2 (
    .in1(decoder_2_out7), .in2(decoder_2_out7), .in3(decoder_2_out7), .in4(decoder_2_out7),
    .in5(decoder_2_out7), .in6(decoder_2_out7), .in7(decoder_2_out7), .out(multiplexer_2_out),
    .sel(joystick_1_y));  // open: in0
  // DotMatrix #(.inputtype("select"), .matrixcols(7)) dotmatrix_1: pin names not known; wires that end beside it: multiplexer_1_out, multiplexer_2_out
endmodule
